# Fritzing sketch merilna_enota (saved by Fritzing 0.9.5d)
circuit board: 3.43696cm x 5.12751cm

parts:
  TP1 = TP4056 [chip_label=TP4056 package="DIP (Dual Inline) [THT]"]
  Mod1 = TTGO T7-ESP32
  Bat1 = battery_holder_dual_18650 [part_number=TBH-18650-2A-P]
  Part1 = INMP441
  U2 = SPDT Slide Switch [package=ayz0202]
  R1 = Resistor [tolerance=±5% resistance=22k package=THT]
  R3 = Resistor [tolerance=±5% resistance=4.7k package=THT]
  Squix1 = OLED 0.91" 128x32 I2C SSD1306 (GND/VCC)

nets:
  N1: TP1.pin3, Mod1.5V, R1.Pin_1
  N2: TP1.pin4, Bat1.+#2, Bat1.+#3
  N3: TP1.pin5, Bat1.+#0, Bat1.+#1
  N4: TP1.pin6, U2.2, U2.5
  GND: Mod1.GND, Part1.GND, U2.3, U2.1, R3.Pin_0, Squix1.GND
  N5: Mod1.VP, R1.Pin_0, R3.Pin_1
  3V3: Mod1.3V3, Part1.L/R, Part1.VDD, Squix1.VCC
  N6: Mod1.TD0, Part1.WS
  N7: Mod1.TDI, Part1.SCK
  N8: Mod1.21, Squix1.SCA
  N9: Mod1.32, Part1.SD
  N10: Mod1.22, Squix1.SCL
  N11: Mod1.27, U2.4

custom parts:
  TP4056: A DIP stand-in part for whatever IC you want. With 6 pins on a 300mil dual inline package (DIP) footprint.
  TTGO T7-ESP32: TTGO T7-ESP32 cpu module
  battery_holder_dual_18650: TBH-18650-2A-P dual 18650 battery holder.
  INMP441: This is a simple breakout board for the INMP441 I2S MEMS microphone.
  OLED 0.91" 128x32 I2C SSD1306 (GND/VCC): OLED 0.91" 128x32 I2C SSD1306 Pinout: GND/VCC/SCL/SDA
