# Fritzing sketch zbirna_enota (saved by Fritzing 0.9.5d)
circuit board: 6.55891cm x 2.99468cm

parts:
  Mod1 = TTGO T7-ESP32
  Mod2 = TTGO T7-ESP32
  Squix2 = OLED 0.91" 128x32 I2C SSD1306 (GND/VCC)
  Squix1 = OLED 0.91" 128x32 I2C SSD1306 (GND/VCC)

nets:
  GND: Mod1.GND, Mod2.GND, Squix2.GND, Squix1.GND
  3V3: Mod1.3V3, Squix1.VCC
  5V: Mod1.5V, Mod2.5V
  N1: Mod1.16, Mod2.17
  N2: Mod1.17, Mod2.16
  N3: Mod1.21, Squix1.SCA
  N4: Mod1.22, Squix1.SCL
  3V3_2: Mod2.3V3, Squix2.VCC
  N5: Mod2.21, Squix2.SCA
  N6: Mod2.22, Squix2.SCL

custom parts:
  TTGO T7-ESP32: TTGO T7-ESP32 cpu module
  OLED 0.91" 128x32 I2C SSD1306 (GND/VCC): OLED 0.91" 128x32 I2C SSD1306 Pinout: GND/VCC/SCL/SDA
